# Fritzing sketch Anel_LED (saved by Fritzing 0.9.3b)

parts:
  neopixel1 = Neopixel 24 Ring
  Componente1 = Arduino Uno (Rev3)

nets:
  VCC: neopixel1.Vcc, Componente1.5V
  N1: neopixel1.IN, Componente1.D7
  GND: neopixel1.GND, Componente1.GND
