# Fritzing sketch GSM_GPRS_CALL_SMS (saved by Fritzing 0.9.3b)

parts:
  Componente1 = Arduino Uno (Rev3)
  GSM_SIM_GPSR_SMS_SIM900_SIM1 = SIM800L [package=THT]

nets:
  N1: Componente1.D2, GSM_SIM_GPSR_SMS_SIM900_SIM1.SIM_TXD
  N2: Componente1.D3_PWM, GSM_SIM_GPSR_SMS_SIM900_SIM1.SIM_RXD
  N3: Componente1.RESET, GSM_SIM_GPSR_SMS_SIM900_SIM1.RST
  5V: Componente1.5V, GSM_SIM_GPSR_SMS_SIM900_SIM1.5V
  GND: Componente1.GND, GSM_SIM_GPSR_SMS_SIM900_SIM1.GND
