# Fritzing sketch GSM_GPRS_HTTP_v2 (saved by Fritzing 0.9.3b)

parts:
  Componente1 = Arduino Uno (Rev3)
  GSM_SIM_GPSR_SMS_SIM900_SIM1 = SIM800L [package=THT]
  Power_plug1 = Power plug

nets:
  N1: Componente1.D10_PWM/SS, GSM_SIM_GPSR_SMS_SIM900_SIM1.SIM_TXD
  N2: Componente1.D11_PWM/MOSI, GSM_SIM_GPSR_SMS_SIM900_SIM1.SIM_RXD
  N3: Componente1.RESET, GSM_SIM_GPSR_SMS_SIM900_SIM1.RST
  5V: GSM_SIM_GPSR_SMS_SIM900_SIM1.5V, Power_plug1.VCC
  GND: GSM_SIM_GPSR_SMS_SIM900_SIM1.GND, Power_plug1.GND

notes:
  5v - 2A
